# Fritzing sketch FirstDevelpopingSchematic (saved by Fritzing 0.8.5b)
breadboards: 1

parts:
  Arduino1 = Arduino Mini (Rev5)
  R1 = Rotary Potentiometer (Small) [maximum_resistance=100kΩ package=THT]
  NEOPIXEL1 = Neopixel Strip -- Black (30/m)

nets:
  N1: Arduino1.D6_PWM, NEOPIXEL1.DO
  GND: Arduino1.GND, R1.leg2, NEOPIXEL1.GND
  N2: Arduino1.A2, R1.wiper
  5V: Arduino1.5V, R1.leg1, NEOPIXEL1.+5V

custom parts:
  Neopixel Strip -- Black (30/m): Neopixel Strip, Black, 30 pixels per meter.
